# Fritzing sketch Switching (saved by Fritzing 0.9.3b)
stripboards: 1

parts:
  Q1 = NPN-Transistor [package="TO92 [THT]"]
  Q3 = NPN-Transistor [package="TO92 [THT]"]
  J3 = male pin header, 2 pins [form="♂ (male)"]
  J1 = male pin header, 2 pins [form="♂ (male)"]
  J2 = male pin header, 2 pins [form="♂ (male)"]
  J4 = male pin header, 3 pins [form="♂ (male)"]
  Q2 = NPN-Transistor [package="TO92 [THT]"]
  J5 = male pin header, 3 pins [form="♂ (male)"]
  J6 = male pin header, 3 pins [form="♂ (male)"]
  J7 = male pin header, 3 pins [form="♂ (male)"]
  J8 = female pin header, 3 pins [form="♀ (female)"]

nets:
  GND: Q1.E, Q3.E, J3.pin2, J1.pin2, J2.pin2, Q2.E, J5.pin1, J6.pin1, J7.pin1
  N1: Q1.B, J4.pin1
  N2: Q1.C, J2.pin1
  N3: Q3.B, J4.pin3
  N4: Q3.C, J1.pin1
  N5: J3.pin1, Q2.C
  N6: J4.pin2, Q2.B
  N7: J5.pin2, J6.pin2, J7.pin2
  N8: J5.pin3, J8.pin1
  N9: J6.pin3, J8.pin2
  N10: J7.pin3, J8.pin3
